# Fritzing sketch servos (saved by Fritzing 0.9.3b)

parts:
  J1 = Basic Servo
  LED1 = LED - 5mm [color="Red (633nm)" package="5 mm [THT]"]
  Part2 = Arduino Sensor Shield v5.0
  Part3 = Arduino Mega 2560 (Rev3)  # not connected
  M3 = Dagu DGServo 9g (Top view) [part_number=RS001B]

nets:
  GND: J1.gnd, Part2.GND#95, Part2.GND#121, Part2.GND#122, M3.gnd
  VCC: J1.vcc, Part2.+5V#94, Part2.+5V#106, Part2.+5V#107, M3.vcc
  N1: J1.pulse, Part2.D9
  N2: LED1.cathode, Part2.GND#144
  N3: LED1.anode, Part2.+5V#90
  N4: Part2.D10, M3.pulse
